// Logisim project CSE332-12bit-CPU.circ as structural Verilog: 4 circuits, main circuit main
module main (
  input  in_1,
  input  in_2,
  output [11:0] r1_Output,
  output [11:0] BinaryCode,
  output [11:0] R2,
  output [11:0] R3
);

  wire alu_1_zero, and_1_out, and_2_out, clock_1_out, control_unit_1_alusrc, control_unit_1_beq,
       control_unit_1_bne, control_unit_1_dispout, control_unit_1_memtoreg, control_unit_1_memwrite,
       control_unit_1_regwrite, not_1_out;
  wire [1:0] multiplexer_3_out, or_1_out;
  wire [2:0] control_unit_1_alucontrol;
  wire [3:0] keyboard_1_data;
  wire [6:4] keyboard_1_data_2;
  wire [11:0] adder_1_out, adder_2_out, alu_1_result, bit_extender_1_out, bit_extender_2_out,
       multiplexer_1_out, multiplexer_2_out, multiplexer_4_out, multiplexer_5_out, ram_1_data, register_1_q;

  Clock clock_1 (.out(clock_1_out));
  Adder #(.width(12)) adder_1 (.a(register_1_q), .b(12'h1), .out(adder_1_out));  // open: cin, cout
  Register #(.width(12)) register_1 (.D(multiplexer_1_out), .Q(register_1_q), .clk(clock_1_out));  // open: en, clr
  Adder #(.width(12)) adder_2 (.a(adder_1_out), .b(bit_extender_1_out), .out(adder_2_out));  // open: cin, cout
  Multiplexer #(.select(2), .width(12)) multiplexer_1 (
    .in0(adder_1_out), .in1(adder_2_out), .in2(bit_extender_2_out), .out(multiplexer_1_out), .sel(or_1_out));  // open: in3, en
  ROM #(.addrWidth(12), .dataWidth(12)) rom_1 (.addr(register_1_q), .data(BinaryCode));  // open: sel
  Control_Unit control_unit_1 (
    .Opcode(BinaryCode[11:8]), .AluControl(control_unit_1_alucontrol), .RegWrite(control_unit_1_regwrite),
    .MemWrite(control_unit_1_memwrite), .BEQ(control_unit_1_beq), .BNE(control_unit_1_bne),
    .Jump(or_1_out[1]), .ALUSrc(control_unit_1_alusrc), .MemToReg(control_unit_1_memtoreg),
    .DispOut(control_unit_1_dispout));  // open: MemRead
  Keyboard keyboard_1 (.clk(in_1), .clr(in_2), .data({keyboard_1_data_2, keyboard_1_data}));  // open: re, avail
  ALU alu_1 (
    .A(R2), .B(multiplexer_2_out), .Shamt(BinaryCode[1:0]), .IN(keyboard_1_data), .Result(alu_1_result),
    .AluControl(control_unit_1_alucontrol), .Zero(alu_1_zero));  // open: in_1
  assign bit_extender_1_out = {{8{1'b0}}, BinaryCode[3:0]};  // Bit_Extender bit_extender_1
  assign bit_extender_2_out = {{4{1'b0}}, BinaryCode[7:0]};  // Bit_Extender bit_extender_2
  _12_bit_register u_12_bit_register_1 (
    .WriteData(multiplexer_4_out), .WriteReg(multiplexer_3_out), .RegWrite(control_unit_1_regwrite),
    .ClK(clock_1_out), .ReadData1(r1_Output), .ReadData1_2(R2), .ReadReg1(BinaryCode[7:6]), .ReadData2(R3),
    .ReadReg2(BinaryCode[5:4]));
  Multiplexer #(.width(12)) multiplexer_2 (
    .in0(R3), .in1(bit_extender_1_out), .out(multiplexer_2_out), .sel(control_unit_1_alusrc));  // open: en
  not not_1 (not_1_out, alu_1_zero);
  Multiplexer #(.width(2)) multiplexer_3 (
    .in0(BinaryCode[3:2]), .in1(2'b01), .out(multiplexer_3_out), .sel(control_unit_1_alusrc));  // open: en
  and and_1 (and_1_out, control_unit_1_beq, alu_1_zero);
  or or_1 (or_1_out[0], and_1_out, and_2_out);
  and and_2 (and_2_out, not_1_out, control_unit_1_bne);
  Multiplexer #(.width(12)) multiplexer_4 (
    .in0(alu_1_result), .in1(ram_1_data), .out(multiplexer_4_out), .sel(control_unit_1_memtoreg));  // open: en
  RAM #(.addrWidth(12), .dataWidth(12), .bus("separate")) ram_1 (
    .addr(alu_1_result), .din(R3), .data(ram_1_data), .str(control_unit_1_memwrite), .clk(clock_1_out));  // open: sel, ld, clr
  Multiplexer #(.width(12)) multiplexer_5 (
    .in1(r1_Output), .out(multiplexer_5_out), .sel(control_unit_1_dispout));  // open: in0, en
  Hex_Digit_Display hex_digit_display_1 (.value(multiplexer_5_out[3:0]));  // open: dp

  // Notes on the sheet:
  //   contents of rom_1 (hex, n*v repeats v):
  //   b4 1b4 2b4 3b4 485 585 695 793 893 962 a62 c04 b0e d08 d04 c04
endmodule

module _12_bit_register (
  input  [11:0] WriteData,
  input  [1:0] ReadReg1,
  input  [1:0] WriteReg,
  input  [1:0] ReadReg2,
  input  RegWrite,
  input  ClK,
  output [11:0] ReadData1,
  output [11:0] ReadData1_2,
  output [11:0] ReadData2
);

  wire and_1_out, and_2_out, and_3_out, decoder_1_out1, decoder_1_out2, decoder_1_out3, Reset_out;
  wire [11:0] R2_q, R3_q;

  Decoder #(.select(2)) decoder_1 (
    .out1(decoder_1_out1), .out2(decoder_1_out2), .out3(decoder_1_out3), .sel(WriteReg));  // open: out0, en
  Clock Reset (.out(Reset_out));
  and and_1 (and_1_out, decoder_1_out1, RegWrite);
  and and_2 (and_2_out, decoder_1_out2, RegWrite);
  and and_3 (and_3_out, decoder_1_out3, RegWrite);
  Register #(.width(12)) R1 (.D(WriteData), .en(and_1_out), .Q(ReadData1), .clk(ClK), .clr(Reset_out));
  Register #(.width(12)) R2 (.D(WriteData), .en(and_2_out), .Q(R2_q), .clk(ClK), .clr(Reset_out));
  Register #(.width(12)) R3 (.D(WriteData), .en(and_3_out), .Q(R3_q), .clk(ClK), .clr(Reset_out));
  Multiplexer #(.select(2), .width(12)) multiplexer_1 (
    .in0({12{1'b0}}), .in1(ReadData1), .in2(R2_q), .in3(R3_q), .out(ReadData1_2), .sel(ReadReg1));  // open: en
  Multiplexer #(.select(2), .width(12)) multiplexer_2 (
    .in0({12{1'b0}}), .in1(ReadData1), .in2(R2_q), .in3(R3_q), .out(ReadData2), .sel(ReadReg2));  // open: en

  // Notes on the sheet:
  //      R0_zero
  //   12 bit Register 
endmodule

module ALU (
  input  in_1,
  input  [11:0] A,
  input  [2:0] AluControl,
  input  [11:0] B,
  input  [1:0] Shamt,
  input  [3:0] IN,
  output [11:0] Result,
  output Zero
);

  wire or_2_out;
  wire [3:0] bit_extender_1_out;
  wire [11:0] adder_1_out, and_1_out, bit_extender_2_out, or_1_out, shifter_1_out, shifter_2_out,
       subtractor_1_out;

  assign bit_extender_1_out = {{2{1'b0}}, Shamt};  // Bit_Extender bit_extender_1
  assign and_1_out = A & B;  // AND_Gate and_1, 12 bits wide
  assign or_1_out = A | B;  // OR_Gate or_1, 12 bits wide
  Shifter #(.width(12)) shifter_1 (.in(A), .\dist (bit_extender_1_out), .out(shifter_1_out));
  Shifter #(.width(12), .shift("lr")) shifter_2 (.in(A), .\dist (bit_extender_1_out), .out(shifter_2_out));
  assign bit_extender_2_out = {{8{1'b0}}, IN};  // Bit_Extender bit_extender_2
  Adder #(.width(12)) adder_1 (.a(A), .b(B), .out(adder_1_out), .cin(in_1));  // open: cout
  Subtractor #(.width(12)) subtractor_1 (.a(A), .b(B), .out(subtractor_1_out));  // open: bin, bout
  Multiplexer #(.select(3), .width(12)) multiplexer_1 (
    .in0(adder_1_out), .in1(subtractor_1_out), .in2(and_1_out), .in3(or_1_out), .in4(shifter_1_out),
    .in5(shifter_2_out), .in6(bit_extender_2_out), .out(Result), .sel(AluControl));  // open: in7, en
  or or_2 (or_2_out, Result[0], Result[1], Result[2], Result[3], Result[4], Result[5], Result[6], Result[7], Result[8], Result[9], Result[10], Result[11]);
  not not_1 (Zero, or_2_out);

  // Notes on the sheet:
  //   12 Bit ALU
endmodule

module Control_Unit (
  input  [3:0] Opcode,
  output [2:0] AluControl,
  output RegWrite,
  output MemRead,
  output MemWrite,
  output BEQ,
  output BNE,
  output Jump,
  output ALUSrc,
  output MemToReg,
  output DispOut
);

  wire decoder_1_out0, decoder_1_out1, decoder_1_out2, decoder_1_out3, decoder_1_out4, decoder_1_out5,
       decoder_1_out6, decoder_1_out12;

  Decoder #(.select(4)) decoder_1 (
    .out0(decoder_1_out0), .out1(decoder_1_out1), .out2(decoder_1_out2), .out3(decoder_1_out3),
    .out4(decoder_1_out4), .out5(decoder_1_out5), .out6(decoder_1_out6), .out7(MemRead), .out8(MemWrite),
    .out9(BEQ), .out10(BNE), .out11(Jump), .out12(decoder_1_out12), .out13(DispOut), .sel(Opcode));  // open: out14, out15, en
  or AluCtrl2 (AluControl[2], decoder_1_out4, decoder_1_out5, decoder_1_out12);
  or AluCtrl1 (AluControl[1], decoder_1_out2, decoder_1_out3, decoder_1_out12);
  or AluCtrl0 (AluControl[0], decoder_1_out1, decoder_1_out3, decoder_1_out5, BEQ, BNE);
  or or_1 (ALUSrc, decoder_1_out6, MemRead, MemWrite);
  or or_2 (RegWrite, decoder_1_out0, decoder_1_out1, decoder_1_out2, decoder_1_out3, decoder_1_out4, decoder_1_out5, decoder_1_out6, MemRead, decoder_1_out12);

  assign MemToReg = MemRead;

  // Notes on the sheet:
  //   Control Unit
endmodule
